// Logisim project CPU.circ as structural Verilog: 1 circuit, main circuit main
module main (
  input  [3:0] Din,
  input  [2:0] R,
  input  Read,
  input  Write,
  input  [2:0] Rx,
  input  [2:0] Ry,
  input  [2:0] Sel,
  output [3:0] out_8
);

  wire [3:0] regfile_1_sx, regfile_1_sy;

  RegFile regfile_1 (
    .RegNbr(R), .Sx(regfile_1_sx), .Sy(regfile_1_sy), .Write(Write), .Read(Read), .Din(Din), .Ry(Ry), .Rx(Rx));
  ALU_PROC alu_proc_1 (.S(Sel), .in_1(regfile_1_sx), .in_2(regfile_1_sy), .out_6(out_8));  // open: Ci, Co
endmodule
