// Logisim project REGISTER.circ as structural Verilog
// REGISTER
module REGISTER_4_bits (
  input  [3:0] D,
  input  CLK,
  input  READ,
  output [3:0] out_4
);

  wire D0_s, D1_s, D2_s, D3_s;

  D_Flip_Flop D3 (.S(D3_s), .D(D[3]), .CLK(CLK));  // open: S_B
  and and_1 (out_4[3], READ, D3_s);
  D_Flip_Flop D2 (.S(D2_s), .D(D[2]), .CLK(CLK));  // open: S_B
  and and_2 (out_4[2], READ, D2_s);
  D_Flip_Flop D1 (.S(D1_s), .D(D[1]), .CLK(CLK));  // open: S_B
  and and_3 (out_4[1], READ, D1_s);
  D_Flip_Flop D0 (.S(D0_s), .D(D[0]), .CLK(CLK));  // open: S_B
  and and_4 (out_4[0], READ, D0_s);
endmodule
